# Fritzing sketch esp32_system (saved by Fritzing 1.0.1rc)
breadboards: 1

parts:
  U1 = ESP32S-HiLetgo [part_number=ESP32S-HiLetgo]
  M1 = ph-4502c [package=THT]
  A1 = tds-sensor-meter-v1.0_1
  R1 = Rotary Potentiometer (Small) [maximum_resistance=10kΩ knob_status=50% power=0.5W package=THT]
  R2 = Rotary Potentiometer (Small) [maximum_resistance=10kΩ knob_status=50% power=0.5W package=THT]

nets:
  N1: U1.3.3, A1.pin2
  N2: U1.GPIO34, A1.pin1
  N3: U1.GPIO32, R1.wiper
  N4: U1.GPIO33, R2.wiper
  N5: U1.GND, M1.pin5, A1.pin3, R1.leg2, R2.leg2
  N6: U1.VIN, M1.pin6
  N7: M1.pin1, R2.leg1
  N8: M1.pin3, R1.leg1

custom parts:
  ESP32S-HiLetgo: HiLetgo ESP-WROOM-32 ESP32 ESP-32S Development Board 2.4GHz Dual-Mode WiFi + Bluetooth Dual Cores Microcontroller The ESP32 integrated with Antenna switches, RF Balun, power amplifiers, low-noise amplifiers, filters, and management modules, and the entire solution occupies the least area of PCB. 2.4 GHz Wi-Fi plus Bluetooth dual-mode chip, with TSMC Ultra-low power consumption 40nm technology,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
  ph-4502c: ph-4502c PH Meter.
  : TDS Meter V1.0 Development Board Water Meter Filter Measuring Water Sensor Module.
